// Logisim project BitCastleDefense.circ as structural Verilog: 13 circuits, main circuit main
module main (
);

  wire and_2_out, b11, b12, b21, b22, b31, b32, b41, b42, Bflag, boss, c11, c12, c21, c22, c31, c32, c41,
       c42, clear, Clk, comparator_1_gt, comparator_2_eq, comparator_3_eq, comparator_3_gt, comparator_4_eq,
       comparator_4_gt, demultiplexer_1_out0, demultiplexer_1_out1, demultiplexer_1_out2,
       demultiplexer_1_out3, demultiplexer_3_out0, demultiplexer_3_out1, demultiplexer_3_out2,
       demultiplexer_3_out3, Die, DOWN_out, e11, e12, e21, e22, e31, e32, e41, e42, ED1, ED2, ED3, ED4, ED11,
       ED22, ED33, ED44, Epos1, Epos2, Epos3, Epos4, gen1_1_genon, gen2_1_genon, gen3_1_genon, gen4_1_genon,
       k1, k2, k3, k4, MD1, MD2, MD3, MD4, not_1_out, or_1_out, or_3_out, or_4_out, or_10_out, pos1, pos2,
       pos3, pos4, R, RStop, shooting, StageFin, Stop, UP_out;
  wire [1:0] Stage, undriven, up_down_1_out_3;
  wire [2:0] Bcnt;
  wire [3:0] adder_1_out, bit_extender_1_out, counter_1_q, EnmyHit, multiplexer_1_out, myHit;
  wire [4:0] adder_2_out, adder_3_out, adder_4_out, adder_5_out, adder_6_out, adder_8_out, B, counter_2_q,
       counter_3_q, counter_4_q, counter_5_q, counter_6_q, counter_7_q, counter_8_q, counter_9_q, mLifeNum,
       multiplexer_2_out;
  wire [9:0] display_dot_1_o1, display_dot_1_o2, display_dot_1_o3, display_dot_1_o4, display_dot_1_o5,
       display_dot_1_o6, display_dot_1_o7, display_dot_1_o8, display_dot_1_o9, display_dot_1_o10,
       display_dot_1_o11, display_dot_1_o12, display_dot_1_o13, display_dot_1_o14, display_dot_1_o15,
       display_dot_1_o16;
  wire [15:0] EnemyHP, LIFE, m1, m2, m3, m4;

  or or_1 (or_1_out, Die, clear);
  or or_2 (RStop, R, Stop);
  Comparator #(.mode("unsigned"), .width(3)) comparator_1 (.a(Bcnt), .b(3'b000), .gt(comparator_1_gt));  // open: eq, lt
  and and_1 (Stop, or_1_out, ~R);  // AND_Gate
  and and_2 (and_2_out, shooting, comparator_1_gt);
  Demultiplexer #(.select(2)) demultiplexer_1 (
    .out0(demultiplexer_1_out0), .out1(demultiplexer_1_out1), .out2(demultiplexer_1_out2),
    .out3(demultiplexer_1_out3), .in(and_2_out), .sel(up_down_1_out_3));
  Clock clock_1 (.out(Clk));
  DotMatrix #(.matrixcols(16), .matrixrows(10)) dotmatrix_1 (
    .col0(display_dot_1_o1), .col1(display_dot_1_o5), .col2(display_dot_1_o9), .col3(display_dot_1_o13),
    .col4(display_dot_1_o2), .col5(display_dot_1_o6), .col6(display_dot_1_o10), .col7(display_dot_1_o14),
    .col8(display_dot_1_o3), .col9(display_dot_1_o7), .col10(display_dot_1_o11), .col11(display_dot_1_o15),
    .col12(display_dot_1_o4), .col13(display_dot_1_o8), .col14(display_dot_1_o12), .col15(display_dot_1_o16));
  Display_dot display_dot_1 (
    .mhp(mLifeNum), .die(Die), .clear(clear), .o1(display_dot_1_o1), .o5(display_dot_1_o5),
    .o9(display_dot_1_o9), .o13(display_dot_1_o13), .o2(display_dot_1_o2), .o6(display_dot_1_o6),
    .o10(display_dot_1_o10), .o14(display_dot_1_o14), .o3(display_dot_1_o3), .o7(display_dot_1_o7),
    .o11(display_dot_1_o11), .o15(display_dot_1_o15), .o4(display_dot_1_o4), .o8(display_dot_1_o8),
    .o12(display_dot_1_o12), .o16(display_dot_1_o16));
  Gen1 gen1_1 (.R(RStop), .genOn(gen1_1_genon));
  Cool8Gen cool8gen_1 (.i1(gen1_1_genon), .o1(e11), .o2(e12));
  Gen2 gen2_1 (.R(RStop), .genOn(gen2_1_genon));
  Cool8Gen cool8gen_2 (.i1(gen2_1_genon), .o1(e21), .o2(e22));
  Gen3 gen3_1 (.R(RStop), .genOn(gen3_1_genon));
  Cool8Gen cool8gen_3 (.i1(gen3_1_genon), .o1(e31), .o2(e32));
  Gen4 gen4_1 (.R(RStop), .genOn(gen4_1_genon));
  Cool8Gen cool8gen_4 (.i1(gen4_1_genon), .o1(e41), .o2(e42));
  up_down up_down_1 (.up(UP_out), .down(DOWN_out), .out_3(up_down_1_out_3));
  Selectbullet selectbullet_1 (.i1(demultiplexer_1_out0), .c1(c11), .c2(c12), .o1(b11), .o2(b12));
  Selectbullet selectbullet_2 (.i1(demultiplexer_1_out1), .c1(c21), .c2(c22), .o1(b21), .o2(b22));
  Selectbullet selectbullet_3 (.i1(demultiplexer_1_out2), .c1(c31), .c2(c32), .o1(b31), .o2(b32));
  Selectbullet selectbullet_4 (.i1(demultiplexer_1_out3), .c1(c41), .c2(c42), .o1(b41), .o2(b42));
  Button Restart (.out(R));
  DotMatrix #(.inputtype("row"), .matrixcols(16), .matrixrows(1)) dotmatrix_2 (.row0(EnemyHP));
  DotMatrix #(.inputtype("row"), .matrixcols(1), .matrixrows(4)) dotmatrix_3 (
    .row0(pos1), .row1(pos2), .row2(pos3), .row3(pos4));
  DotMatrix #(.dotshape("circle"), .inputtype("row"), .matrixcols(16), .matrixrows(1)) dotmatrix_4 (.row0(m1));
  DotMatrix #(.dotshape("circle"), .inputtype("row"), .matrixcols(16), .matrixrows(1)) dotmatrix_5 (.row0(m2));
  DotMatrix #(.dotshape("circle"), .inputtype("row"), .matrixcols(16), .matrixrows(1)) dotmatrix_6 (.row0(m3));
  DotMatrix #(.dotshape("circle"), .inputtype("row"), .matrixcols(16), .matrixrows(1)) dotmatrix_7 (.row0(m4));
  DotMatrix #(.inputtype("row"), .matrixcols(16), .matrixrows(1)) dotmatrix_8 (.row0(LIFE));
  Button UP (.out(UP_out));
  Button DOWN (.out(DOWN_out));
  or or_3 (or_3_out, b11, b12, b21, b22);
  or or_4 (or_4_out, b31, b32, b41, b42);
  assign bit_extender_1_out = {{2{1'b0}}, Stage};  // Bit_Extender bit_extender_1
  Button Attack (.out(shooting));
  Demultiplexer #(.select(2)) demultiplexer_2 (
    .out0(pos1), .out1(pos2), .out2(pos3), .out3(pos4), .in(1'b1), .sel(up_down_1_out_3));
  or or_5 (Bflag, or_3_out, or_4_out);
  Random #(.width(2)) random_1 ();  // open: clk, next, out, clr
  Adder #(.width(4)) adder_1 (.a(4'b0001), .b(bit_extender_1_out), .out(adder_1_out));  // open: cin, cout
  DotMatrix #(.inputtype("row"), .matrixcols(1), .matrixrows(4)) dotmatrix_9 (
    .row0(Epos1), .row1(Epos2), .row2(Epos3), .row3(Epos4));
  // LedBar #(.inputtype("row"), .matrixcols(5)) Ammo: pin names not known; wires that end beside it: B
  Demultiplexer #(.select(2)) demultiplexer_3 (
    .out0(demultiplexer_3_out0), .out1(demultiplexer_3_out1), .out2(demultiplexer_3_out2),
    .out3(demultiplexer_3_out3), .in(boss), .sel(undriven));
  Comparator #(.mode("unsigned"), .width(4)) comparator_2 (
    .a(4'b0111), .b(counter_1_q), .eq(comparator_2_eq));  // open: gt, lt
  Counter #(.max('hf), .width(4)) counter_1 (.Q(counter_1_q), .clk(Clk));  // open: load, D, count, carry, up, clr
  Multiplexer #(.width(4)) multiplexer_1 (.in0(adder_1_out), .in1(4'b1100), .out(multiplexer_1_out), .sel(clear));
  Hex_Digit_Display u_Stage (.value(multiplexer_1_out));  // open: dp
  not not_1 (not_1_out, boss);
  or or_6 (Epos1, not_1_out, demultiplexer_3_out0);
  or or_7 (Epos2, not_1_out, demultiplexer_3_out1);
  or or_8 (Epos3, not_1_out, demultiplexer_3_out2);
  or or_9 (Epos4, not_1_out, demultiplexer_3_out3);
  bullet bullet_1 (.Start(RStop), .bulletBtn(Bflag), .CLK(Clk), .bullet_bar(B), .BulletCnt(Bcnt));
  Map1 map1_1 (
    .e1(e11), .e2(e12), .b1(b11), .b2(b12), .Clk(Clk), .R(RStop), .m(m1), .k1(k1), .EmDmg(ED1), .myDmg(MD1),
    .c1(c11), .c2(c12));
  Map1 map1_2 (
    .e1(e21), .e2(e22), .b1(b21), .b2(b22), .Clk(Clk), .R(RStop), .m(m2), .k1(k2), .EmDmg(ED2), .myDmg(MD2),
    .c1(c21), .c2(c22));
  Map1 map1_3 (
    .e1(e31), .e2(e32), .b1(b31), .b2(b32), .Clk(Clk), .R(RStop), .m(m3), .k1(k3), .EmDmg(ED3), .myDmg(MD3),
    .c1(c31), .c2(c32));
  Map1 map1_4 (
    .e1(e41), .e2(e42), .b1(b41), .b2(b42), .Clk(Clk), .R(RStop), .m(m4), .k1(k4), .EmDmg(ED4), .myDmg(MD4),
    .c1(c41), .c2(c42));
  Counter #(.max('h1f), .width(5)) counter_2 (
    .count(1'b1), .Q(counter_2_q), .clk(MD1), .clr(R));  // open: load, D, carry, up
  Counter #(.max('h1f), .width(5)) counter_3 (
    .count(1'b1), .Q(counter_3_q), .clk(MD2), .clr(R));  // open: load, D, carry, up
  Counter #(.max('h1f), .width(5)) counter_4 (
    .count(1'b1), .Q(counter_4_q), .clk(MD3), .clr(R));  // open: load, D, carry, up
  Counter #(.max('h1f), .width(5)) counter_5 (
    .count(1'b1), .Q(counter_5_q), .clk(MD4), .clr(R));  // open: load, D, carry, up
  Counter #(.max('h1f), .width(5)) counter_6 (
    .count(1'b1), .Q(counter_6_q), .clk(ED11), .clr(or_10_out));  // open: load, D, carry, up
  Counter #(.max('h1f), .width(5)) counter_7 (
    .count(1'b1), .Q(counter_7_q), .clk(ED22), .clr(or_10_out));  // open: load, D, carry, up
  Counter #(.max('h1f), .width(5)) counter_8 (
    .count(1'b1), .Q(counter_8_q), .clk(ED33), .clr(or_10_out));  // open: load, D, carry, up
  Counter #(.max('h1f), .width(5)) counter_9 (
    .count(1'b1), .Q(counter_9_q), .clk(ED44), .clr(or_10_out));  // open: load, D, carry, up
  Multiplexer #(.select(2), .width(5)) multiplexer_2 (
    .in0(5'b01000), .in1({5{1'b0}}), .in2(5'b01000), .in3(5'b01111), .out(multiplexer_2_out), .sel(Stage));
  Adder #(.width(5)) adder_2 (.a(counter_2_q), .b(counter_3_q), .out(adder_2_out));  // open: cin, cout
  Adder #(.width(5)) adder_3 (.a(counter_4_q), .b(counter_5_q), .out(adder_3_out));  // open: cin, cout
  Adder #(.width(5)) adder_4 (.a(counter_6_q), .b(counter_7_q), .out(adder_4_out));  // open: cin, cout
  Adder #(.width(5)) adder_5 (.a(counter_8_q), .b(adder_6_out), .out(adder_5_out));  // open: cin, cout
  Adder #(.width(5)) adder_6 (.a(counter_9_q), .b(multiplexer_2_out), .out(adder_6_out));  // open: cin, cout
  Adder #(.width(5)) adder_7 (.a(adder_2_out), .b(adder_3_out), .out(mLifeNum));  // open: cin, cout
  Comparator #(.mode("unsigned"), .width(5)) comparator_3 (
    .a(mLifeNum), .b(5'b10000), .gt(comparator_3_gt), .eq(comparator_3_eq));  // open: lt
  or or_10 (or_10_out, Stop, StageFin);
  Adder #(.width(5)) adder_8 (.a(adder_4_out), .b(adder_5_out), .out(adder_8_out));  // open: cin, cout
  Comparator #(.mode("unsigned"), .width(5)) comparator_4 (
    .a(adder_8_out), .b(5'b10000), .gt(comparator_4_gt), .eq(comparator_4_eq));  // open: lt
  Bit_Extender #(.in_width(5), .out_width(4), .\type ("zero")) bit_extender_2 (.in(mLifeNum), .out(myHit));
  or or_11 (Die, comparator_3_gt, comparator_3_eq);
  Bit_Extender #(.in_width(5), .out_width(4), .\type ("zero")) bit_extender_3 (.in(adder_8_out), .out(EnmyHit));
  or or_12 (StageFin, comparator_4_gt, comparator_4_eq);
  HP hp_1 (.Hit(myHit), .fin(Die), .H(LIFE));
  HP hp_2 (.Hit(EnmyHit), .fin(clear), .H(EnemyHP));
  Counter #(.max('h3), .width(2)) counter_10 (
    .count(1'b1), .Q(Stage), .clk(StageFin), .clr(R));  // open: load, D, carry, up
  Comparator #(.mode("unsigned"), .width(2)) comparator_5 (.a(Stage), .b(2'b10), .gt(clear), .eq(boss));  // open: lt
  and and_3 (ED11, ED1, Epos1);
  and and_4 (ED22, ED2, Epos2);
  and and_5 (ED33, ED3, Epos3);
  and and_6 (ED44, ED4, Epos4);

  // Notes on the sheet:
  //   3Stage
endmodule

module Map1 (
  input  e1,
  input  e2,
  input  b1,
  input  b2,
  input  Clk,
  input  R,
  output [15:0] m,
  output k1,
  output EmDmg,
  output myDmg,
  output c1,
  output c2
);

  wire A, and_1_out, and_2_out, and_3_out, and_4_out, and_5_out, and_6_out, B, buffer_1_out, buffer_2_out, C,
       comparator_1_gt, comparator_2_gt, comparator_3_gt, comparator_4_gt, comparator_5_gt, comparator_6_eq,
       comparator_7_gt, comparator_8_gt, comparator_9_eq, comparator_10_gt, counter_1_carry, counter_2_carry,
       counter_3_carry, counter_4_carry, D, En1, En2, my1, my2, or_1_out, or_2_out, or_3_out, or_4_out,
       or_5_out, or_6_out, or_7_out, or_8_out, or_9_out, or_10_out, or_13_out, or_14_out, or_15_out,
       or_16_out, or_17_out, or_18_out, or_19_out, or_20_out;
  wire [3:0] counter_1_q, counter_2_q, counter_3_q, counter_4_q, not_1_out, not_2_out, not_3_out, not_4_out;
  wire [15:0] shifter_1_out, shifter_2_out, shifter_3_out, shifter_4_out;

  or or_1 (or_1_out, and_1_out, buffer_1_out);
  and and_1 (and_1_out, Clk, comparator_1_gt);
  or or_2 (or_2_out, and_2_out, buffer_2_out);
  and and_2 (and_2_out, Clk, comparator_2_gt);
  Counter #(.max('hf), .width(4)) counter_1 (
    .D(4'b0001), .Q(counter_1_q), .carry(counter_1_carry), .clk(Clk), .clr(or_3_out));  // open: load, count, up
  or or_3 (or_3_out, or_13_out, R, ~or_4_out);  // OR_Gate
  or or_4 (or_4_out, comparator_3_gt, e1);
  Counter #(.max('hf), .width(4)) counter_2 (
    .D(4'b0001), .Q(counter_2_q), .carry(counter_2_carry), .clk(Clk), .clr(or_5_out));  // open: load, count, up
  or or_5 (or_5_out, or_14_out, R, ~or_6_out);  // OR_Gate
  or or_6 (or_6_out, comparator_4_gt, e2);
  Counter #(.max('hf), .width(4)) counter_3 (
    .D(4'b0001), .Q(counter_3_q), .carry(counter_3_carry), .clk(or_1_out), .clr(or_7_out));  // open: load, count, up
  or or_7 (or_7_out, or_15_out, ~or_8_out);  // OR_Gate
  or or_8 (or_8_out, b1, comparator_1_gt);
  buf buffer_1 (buffer_1_out, b1);
  Counter #(.max('hf), .width(4)) counter_4 (
    .D(4'b0001), .Q(counter_4_q), .carry(counter_4_carry), .clk(or_2_out), .clr(or_9_out));  // open: load, count, up
  or or_9 (or_9_out, or_16_out, ~or_10_out);  // OR_Gate
  or or_10 (or_10_out, b2, comparator_2_gt);
  buf buffer_2 (buffer_2_out, b2);
  or or_11 (EmDmg, En1, En2);
  or or_12 (myDmg, my1, my2);
  or or_13 (or_13_out, counter_1_carry, A, C);
  buf buffer_3 (my1, counter_1_carry);
  or or_14 (or_14_out, counter_2_carry, B, D);
  buf buffer_4 (my2, counter_2_carry);
  buf buffer_5 (En1, counter_3_carry);
  or or_15 (or_15_out, or_17_out, R);
  buf buffer_6 (En2, counter_4_carry);
  or or_16 (or_16_out, or_19_out, R);
  or or_17 (or_17_out, counter_3_carry, or_18_out);
  or or_18 (or_18_out, A, B);
  or or_19 (or_19_out, counter_4_carry, or_20_out);
  or or_20 (or_20_out, C, D);
  Comparator #(.mode("unsigned"), .width(4)) comparator_1 (
    .a(counter_3_q), .b(4'b0000), .gt(comparator_1_gt), .eq(c1));  // open: lt
  Comparator #(.mode("unsigned"), .width(4)) comparator_2 (
    .a(counter_4_q), .b(4'b0000), .gt(comparator_2_gt), .eq(c2));  // open: lt
  Comparator #(.mode("unsigned"), .width(4)) comparator_3 (
    .a(counter_1_q), .b(4'b0000), .gt(comparator_3_gt));  // open: eq, lt
  Comparator #(.mode("unsigned"), .width(4)) comparator_4 (
    .a(counter_2_q), .b(4'b0000), .gt(comparator_4_gt));  // open: eq, lt
  Shifter #(.shift("lr"), .width(16)) shifter_1 (.in(16'h4000), .\dist (not_1_out), .out(shifter_1_out));
  assign not_1_out = ~counter_1_q;  // NOT_Gate not_1, 4 bits wide
  Shifter #(.shift("lr"), .width(16)) shifter_2 (.in(16'h4000), .\dist (not_2_out), .out(shifter_2_out));
  assign not_2_out = ~counter_2_q;  // NOT_Gate not_2, 4 bits wide
  Shifter #(.width(16)) shifter_3 (.in(16'h1), .\dist (not_3_out), .out(shifter_3_out));
  assign not_3_out = ~counter_3_q;  // NOT_Gate not_3, 4 bits wide
  assign not_4_out = ~counter_4_q;  // NOT_Gate not_4, 4 bits wide
  Shifter #(.width(16)) shifter_4 (.in(16'h1), .\dist (not_4_out), .out(shifter_4_out));
  assign m = shifter_1_out | shifter_2_out | shifter_3_out | shifter_4_out;  // OR_Gate or_21, 16 bits wide
  Comparator #(.width(16)) comparator_5 (.a(shifter_1_out), .b(shifter_3_out), .gt(comparator_5_gt));  // open: eq, lt
  Comparator #(.width(16)) comparator_6 (.a(shifter_3_out), .b(16'h8000), .eq(comparator_6_eq));  // open: gt, lt
  Comparator #(.width(16)) comparator_7 (.a(shifter_2_out), .b(shifter_3_out), .gt(comparator_7_gt));  // open: eq, lt
  Comparator #(.width(16)) comparator_8 (.a(shifter_1_out), .b(shifter_4_out), .gt(comparator_8_gt));  // open: eq, lt
  Comparator #(.width(16)) comparator_9 (.a(shifter_4_out), .b(16'h8000), .eq(comparator_9_eq));  // open: gt, lt
  Comparator #(.width(16)) comparator_10 (.a(shifter_2_out), .b(shifter_4_out), .gt(comparator_10_gt));  // open: eq, lt
  and and_3 (and_3_out, comparator_5_gt, ~comparator_6_eq);  // AND_Gate
  and and_4 (and_4_out, comparator_7_gt, ~comparator_6_eq);  // AND_Gate
  and and_5 (and_5_out, comparator_8_gt, ~comparator_9_eq);  // AND_Gate
  and and_6 (and_6_out, comparator_10_gt, ~comparator_9_eq);  // AND_Gate
  buf buffer_7 (k1, and_3_out);
  buf buffer_8 (A, and_3_out);
  buf buffer_9 (k1, and_4_out);
  buf buffer_10 (B, and_4_out);
  buf buffer_11 (k1, and_5_out);
  buf buffer_12 (C, and_5_out);
  buf buffer_13 (k1, and_6_out);
  buf buffer_14 (D, and_6_out);

  // Notes on the sheet:
  //   위는 적, 아래는 총알
endmodule

module HP (
  input  [3:0] Hit,
  input  fin,
  output [15:0] H
);

  wire [3:0] not_1_out, subtractor_1_out;
  wire [15:0] shifter_1_out;

  Subtractor #(.width(4)) subtractor_1 (.a(4'b1111), .b(Hit), .out(subtractor_1_out));  // open: bin, bout
  assign not_1_out = ~subtractor_1_out;  // NOT_Gate not_1, 4 bits wide
  Shifter #(.width(16)) shifter_1 (.in({16{1'b1}}), .\dist (not_1_out), .out(shifter_1_out));
  Multiplexer #(.width(16)) multiplexer_1 (.in0(shifter_1_out), .in1({16{1'b0}}), .out(H), .sel(fin));
endmodule

module bullet (
  input  Start,
  input  bulletBtn,
  input  CLK,
  output [4:0] bullet_bar,
  output [2:0] BulletCnt
);

  wire and_1_out, comparator_1_eq, comparator_1_gt, counter_1_q, or_1_out;
  wire [2:0] adder_1_out, bit_extender_1_out, bit_extender_2_out, subtractor_1_out, subtractor_2_out;

  Counter #(.max('h1), .width(1)) counter_1 (.Q(counter_1_q), .clk(CLK));  // open: load, D, count, carry, up, clr
  Comparator #(.mode("unsigned"), .width(3)) comparator_1 (
    .a(BulletCnt), .b(3'b101), .gt(comparator_1_gt), .eq(comparator_1_eq));  // open: lt
  or or_1 (or_1_out, comparator_1_eq, comparator_1_gt);
  assign bit_extender_1_out = {{2{1'b0}}, and_1_out};  // Bit_Extender bit_extender_1
  and and_1 (and_1_out, counter_1_q, ~or_1_out);  // AND_Gate
  assign bit_extender_2_out = {{2{1'b0}}, bulletBtn};  // Bit_Extender bit_extender_2
  Adder #(.width(3)) adder_1 (.a(bit_extender_1_out), .b(subtractor_1_out), .out(adder_1_out));  // open: cin, cout
  Subtractor #(.width(3)) subtractor_1 (
    .a(BulletCnt), .b(bit_extender_2_out), .out(subtractor_1_out));  // open: bin, bout
  Subtractor #(.width(3)) subtractor_2 (.a(3'b101), .b(BulletCnt), .out(subtractor_2_out));  // open: bin, bout
  Shifter #(.width(5)) shifter_1 (.in({5{1'b1}}), .\dist (subtractor_2_out), .out(bullet_bar));
  RegisterVer2 registerver2_1 (.D(adder_1_out), .CLK(CLK), .R(Start), .Btn(bulletBtn), .Q(BulletCnt));

  // Other names for the same wires on the sheet: Btn = bulletBtn

  // Notes on the sheet:
  //   <  <  <  <
endmodule

module RegisterVer2 (
  input  [2:0] D,
  input  CLK,
  input  R,
  input  Btn,
  output [2:0] Q
);

  wire and_1_out, comparator_1_eq, multiplexer_1_out, multiplexer_2_out, not_1_out;
  wire [2:0] multiplexer_3_out, subtractor_1_out;

  Comparator #(.mode("unsigned"), .width(3)) comparator_1 (.a(3'b000), .b(Q), .eq(comparator_1_eq));  // open: gt, lt
  and and_1 (and_1_out, Btn, ~comparator_1_eq);  // AND_Gate
  Subtractor #(.width(3)) subtractor_1 (.a(Q), .b(3'b001), .out(subtractor_1_out));  // open: bin, bout
  not not_1 (not_1_out, CLK);
  Multiplexer multiplexer_1 (.in0(CLK), .in1(not_1_out), .out(multiplexer_1_out), .sel(and_1_out));
  Multiplexer multiplexer_2 (.in0(multiplexer_1_out), .in1(and_1_out), .out(multiplexer_2_out), .sel(and_1_out));
  Multiplexer #(.width(3)) multiplexer_3 (.in0(D), .in1(subtractor_1_out), .out(multiplexer_3_out), .sel(and_1_out));
  Register #(.width(3)) register_1 (.D(multiplexer_3_out), .clk(multiplexer_2_out), .Q(Q), .clr(R));  // open: en
endmodule

module Selectbullet (
  input  i1,
  input  c1,
  input  c2,
  output o1,
  output o2
);

  wire and_1_out, and_4_out, clock_1_out, clock_2_out, comparator_1_eq, comparator_1_gt, comparator_2_eq,
       comparator_2_gt, or_1_out, or_2_out;
  wire [1:0] counter_1_q, counter_2_q;

  Clock clock_1 (.out(clock_1_out));
  Clock clock_2 (.out(clock_2_out));
  Counter #(.max('h2), .width(2)) counter_1 (
    .count(1'b1), .Q(counter_1_q), .clk(or_1_out));  // open: load, D, carry, up, clr
  or or_1 (or_1_out, and_1_out, o2);
  and and_1 (and_1_out, clock_1_out, comparator_1_gt);
  and and_2 (o1, i1, c1, comparator_1_eq);
  and and_3 (o2, ~c1, i1, c2, comparator_2_eq);  // AND_Gate
  Counter #(.max('h2), .width(2)) counter_2 (
    .count(1'b1), .Q(counter_2_q), .clk(or_2_out));  // open: load, D, carry, up, clr
  or or_2 (or_2_out, and_4_out, o1);
  and and_4 (and_4_out, clock_2_out, comparator_2_gt);
  Comparator #(.mode("unsigned"), .width(2)) comparator_1 (
    .a(counter_1_q), .b(2'b00), .gt(comparator_1_gt), .eq(comparator_1_eq));  // open: lt
  Comparator #(.mode("unsigned"), .width(2)) comparator_2 (
    .a(counter_2_q), .b(2'b00), .gt(comparator_2_gt), .eq(comparator_2_eq));  // open: lt
endmodule

module Gen1 (
  input  R,
  output genOn
);

  wire clock_1_out, clock_2_out, not_1_out;
  wire [1:0] adder_1_out, random_1_out;
  wire [4:0] adder_2_out, bit_extender_1_out, multiplexer_1_out, register_1_q, subtractor_1_out;

  Random #(.seed(1), .width(2)) random_1 (.clk(clock_1_out), .out(random_1_out));  // open: clr, next
  Clock clock_1 (.out(clock_1_out));
  Adder #(.width(2)) adder_1 (.a(2'b01), .b(random_1_out), .out(adder_1_out));  // open: cin, cout
  Multiplexer #(.width(5)) multiplexer_1 (.in0(5'b10000), .in1({5{1'b0}}), .out(multiplexer_1_out), .sel(not_1_out));
  not not_1 (not_1_out, genOn);
  Comparator #(.mode("unsigned"), .width(5)) comparator_1 (.a(5'b10000), .b(register_1_q), .lt(genOn));  // open: gt, eq
  assign bit_extender_1_out = {{3{1'b0}}, adder_1_out};  // Bit_Extender bit_extender_1
  Subtractor #(.width(5)) subtractor_1 (
    .a(register_1_q), .b(multiplexer_1_out), .out(subtractor_1_out));  // open: bin, bout
  Register #(.trigger("falling"), .width(5)) register_1 (
    .D(adder_2_out), .clk(clock_2_out), .Q(register_1_q), .clr(R));  // open: en
  Adder #(.width(5)) adder_2 (.a(bit_extender_1_out), .b(subtractor_1_out), .out(adder_2_out));  // open: cin, cout
  Clock clock_2 (.out(clock_2_out));
endmodule

module Gen2 (
  input  R,
  output genOn
);

  wire clock_1_out, clock_2_out, not_1_out;
  wire [1:0] adder_1_out, random_1_out;
  wire [7:0] adder_2_out, bit_extender_1_out, multiplexer_1_out, register_1_q, subtractor_1_out;

  Random #(.seed(2), .width(2)) random_1 (.clk(clock_1_out), .out(random_1_out));  // open: clr, next
  Clock clock_1 (.out(clock_1_out));
  Adder #(.width(2)) adder_1 (.a(2'b01), .b(random_1_out), .out(adder_1_out));  // open: cin, cout
  Multiplexer #(.width(8)) multiplexer_1 (.in0(8'h10), .in1({8{1'b0}}), .out(multiplexer_1_out), .sel(not_1_out));
  not not_1 (not_1_out, genOn);
  Comparator #(.mode("unsigned")) comparator_1 (.a(8'h10), .b(register_1_q), .lt(genOn));  // open: gt, eq
  assign bit_extender_1_out = {{6{1'b0}}, adder_1_out};  // Bit_Extender bit_extender_1
  Subtractor subtractor_1 (.a(register_1_q), .b(multiplexer_1_out), .out(subtractor_1_out));  // open: bin, bout
  Register #(.trigger("falling")) register_1 (
    .D(adder_2_out), .clk(clock_2_out), .Q(register_1_q), .clr(R));  // open: en
  Adder adder_2 (.a(bit_extender_1_out), .b(subtractor_1_out), .out(adder_2_out));  // open: cin, cout
  Clock clock_2 (.out(clock_2_out));
endmodule

module Gen3 (
  input  R,
  output genOn
);

  wire clock_1_out, clock_2_out, not_1_out;
  wire [1:0] adder_1_out, random_1_out;
  wire [7:0] adder_2_out, bit_extender_1_out, multiplexer_1_out, register_1_q, subtractor_1_out;

  Random #(.seed(3), .width(2)) random_1 (.clk(clock_1_out), .out(random_1_out));  // open: clr, next
  Clock clock_1 (.out(clock_1_out));
  Adder #(.width(2)) adder_1 (.a(2'b01), .b(random_1_out), .out(adder_1_out));  // open: cin, cout
  Multiplexer #(.width(8)) multiplexer_1 (.in0(8'h10), .in1({8{1'b0}}), .out(multiplexer_1_out), .sel(not_1_out));
  not not_1 (not_1_out, genOn);
  Comparator #(.mode("unsigned")) comparator_1 (.a(8'h10), .b(register_1_q), .lt(genOn));  // open: gt, eq
  assign bit_extender_1_out = {{6{1'b0}}, adder_1_out};  // Bit_Extender bit_extender_1
  Subtractor subtractor_1 (.a(register_1_q), .b(multiplexer_1_out), .out(subtractor_1_out));  // open: bin, bout
  Register #(.trigger("falling")) register_1 (
    .D(adder_2_out), .clk(clock_2_out), .Q(register_1_q), .clr(R));  // open: en
  Adder adder_2 (.a(bit_extender_1_out), .b(subtractor_1_out), .out(adder_2_out));  // open: cin, cout
  Clock clock_2 (.out(clock_2_out));
endmodule

module Gen4 (
  input  R,
  output genOn
);

  wire clock_1_out, clock_2_out, not_1_out;
  wire [1:0] adder_1_out, random_1_out;
  wire [7:0] adder_2_out, bit_extender_1_out, multiplexer_1_out, register_1_q, subtractor_1_out;

  Random #(.seed(4), .width(2)) random_1 (.clk(clock_1_out), .out(random_1_out));  // open: clr, next
  Clock clock_1 (.out(clock_1_out));
  Adder #(.width(2)) adder_1 (.a(2'b01), .b(random_1_out), .out(adder_1_out));  // open: cin, cout
  Multiplexer #(.width(8)) multiplexer_1 (.in0(8'h10), .in1({8{1'b0}}), .out(multiplexer_1_out), .sel(not_1_out));
  not not_1 (not_1_out, genOn);
  Comparator #(.mode("unsigned")) comparator_1 (.a(8'h10), .b(register_1_q), .lt(genOn));  // open: gt, eq
  assign bit_extender_1_out = {{6{1'b0}}, adder_1_out};  // Bit_Extender bit_extender_1
  Subtractor subtractor_1 (.a(register_1_q), .b(multiplexer_1_out), .out(subtractor_1_out));  // open: bin, bout
  Register #(.trigger("falling")) register_1 (
    .D(adder_2_out), .clk(clock_2_out), .Q(register_1_q), .clr(R));  // open: en
  Adder adder_2 (.a(bit_extender_1_out), .b(subtractor_1_out), .out(adder_2_out));  // open: cin, cout
  Clock clock_2 (.out(clock_2_out));
endmodule

module Cool8Gen (
  input  i1,
  output o1,
  output o2
);

  wire and_1_out, and_2_out, and_3_out, clock_1_out, comparator_1_gt, comparator_2_eq, comparator_2_gt,
       or_1_out;
  wire [3:0] counter_1_q;

  and and_1 (and_1_out, i1, comparator_2_eq);
  Clock clock_1 (.out(clock_1_out));
  and and_2 (and_2_out, clock_1_out, ~comparator_2_eq);  // AND_Gate
  Counter #(.max('h8), .trigger("falling"), .width(4)) counter_1 (
    .count(1'b1), .Q(counter_1_q), .clk(or_1_out), .clr(o2));  // open: load, D, carry, up
  or or_1 (or_1_out, and_1_out, and_2_out);
  and and_3 (and_3_out, comparator_1_gt, comparator_2_gt);
  Comparator #(.mode("unsigned"), .width(4)) comparator_1 (
    .a(4'b0011), .b(counter_1_q), .gt(comparator_1_gt));  // open: eq, lt
  Comparator #(.mode("unsigned"), .width(4)) comparator_2 (
    .a(counter_1_q), .b(4'b0000), .gt(comparator_2_gt), .eq(comparator_2_eq));  // open: lt
  Comparator #(.mode("unsigned"), .width(4)) comparator_3 (.a(counter_1_q), .b(4'b1000), .eq(o2));  // open: gt, lt
  or or_2 (o1, and_1_out, and_3_out);
endmodule

module up_down (
  input  up,
  input  down,
  output [1:0] out_3
);

  wire [1:0] counter_1_q, counter_2_q;

  Counter #(.max('h3), .width(2)) counter_1 (
    .count(1'b1), .Q(counter_1_q), .clk(down));  // open: load, D, carry, up, clr
  Counter #(.max('h3), .width(2)) counter_2 (.count(1'b1), .Q(counter_2_q), .clk(up));  // open: load, D, carry, up, clr
  Subtractor #(.width(2)) subtractor_1 (.a(counter_1_q), .b(counter_2_q), .out(out_3));  // open: bin, bout
endmodule

module Display_dot (
  input  [4:0] mhp,
  input  die,
  input  clear,
  output [9:0] o1,
  output [9:0] o2,
  output [9:0] o3,
  output [9:0] o4,
  output [9:0] o5,
  output [9:0] o6,
  output [9:0] o7,
  output [9:0] o8,
  output [9:0] o9,
  output [9:0] o10,
  output [9:0] o11,
  output [9:0] o12,
  output [9:0] o13,
  output [9:0] o14,
  output [9:0] o15,
  output [9:0] o16
);

  wire and_1_out, and_2_out, and_3_out, comparator_1_lt, not_1_out, not_2_out, or_1_out;
  wire [1:0] idx;

  Multiplexer #(.select(2), .width(10)) multiplexer_1 (
    .in0(10'h60), .in1(10'h61), .in2(10'h1f1), .in3(10'h28e), .out(o1), .sel(idx));
  Multiplexer #(.select(2), .width(10)) multiplexer_2 (
    .in0(10'h3f), .in1(10'h20), .in2(10'h143), .in3(10'h111), .out(o5), .sel(idx));
  Multiplexer #(.select(2), .width(10)) multiplexer_3 (
    .in0(10'h7f), .in1(10'h33), .in2(10'h141), .in3(10'h291), .out(o9), .sel(idx));
  Multiplexer #(.select(2), .width(10)) multiplexer_4 (
    .in0(10'h3f), .in1(10'h1f), .in2(10'h1e2), .in3({10{1'b0}}), .out(o13), .sel(idx));
  Comparator #(.mode("unsigned"), .width(5)) comparator_1 (
    .a(mhp), .b(5'b01000), .lt(comparator_1_lt));  // open: gt, eq
  not not_1 (not_1_out, comparator_1_lt);
  or or_1 (or_1_out, die, clear);
  not not_2 (not_2_out, or_1_out);
  and and_1 (and_1_out, comparator_1_lt, not_2_out);
  and and_2 (and_2_out, not_2_out, not_1_out);
  and and_3 (and_3_out, die, ~clear);  // AND_Gate
  assign idx = and_1_out ? 2'b00 : 2'bz;  // Controlled_Buffer controlled_buffer_1
  assign idx = and_2_out ? 2'b01 : 2'bz;  // Controlled_Buffer controlled_buffer_2
  assign idx = and_3_out ? 2'b10 : 2'bz;  // Controlled_Buffer controlled_buffer_3
  assign idx = clear ? 2'b11 : 2'bz;  // Controlled_Buffer controlled_buffer_4
  Multiplexer #(.select(2), .width(10)) multiplexer_5 (
    .in0(10'h6f), .in1(10'h3f), .in2(10'h33), .in3(10'h9f), .out(o2), .sel(idx));
  Multiplexer #(.select(2), .width(10)) multiplexer_6 (
    .in0(10'h38f), .in1(10'h8d), .in2({10{1'b0}}), .in3(10'h140), .out(o6), .sel(idx));
  Multiplexer #(.select(2), .width(10)) multiplexer_7 (
    .in0(10'h1fc), .in1(10'h1f8), .in2(10'h1f2), .in3(10'h8e), .out(o10), .sel(idx));
  Multiplexer #(.select(2), .width(10)) multiplexer_8 (
    .in0(10'h3f8), .in1(10'h3f0), .in2(10'h153), .in3(10'h15), .out(o14), .sel(idx));
  Multiplexer #(.select(2), .width(10)) multiplexer_9 (
    .in0(10'h1f8), .in1(10'h190), .in2(10'h151), .in3(10'h14d), .out(o3), .sel(idx));
  Multiplexer #(.select(2), .width(10)) multiplexer_10 (
    .in0(10'h39c), .in1(10'h31c), .in2(10'h111), .in3(10'h80), .out(o7), .sel(idx));
  Multiplexer #(.select(2), .width(10)) multiplexer_11 (
    .in0(10'hf), .in1(10'hf), .in2(10'h3), .in3(10'h14c), .out(o11), .sel(idx));
  Multiplexer #(.select(2), .width(10)) multiplexer_12 (
    .in0(10'h6f), .in1(10'h2b), .in2(10'h180), .in3(10'h12), .out(o15), .sel(idx));
  Multiplexer #(.select(2), .width(10)) multiplexer_13 (
    .in0(10'h3f), .in1(10'h3f), .in2(10'h135), .in3(10'hf), .out(o4), .sel(idx));
  Multiplexer #(.select(2), .width(10)) multiplexer_14 (
    .in0(10'h7f), .in1(10'h7f), .in2(10'h160), .in3(10'h100), .out(o8), .sel(idx));
  Multiplexer #(.select(2), .width(10)) multiplexer_15 (
    .in0(10'h30), .in1(10'h20), .in2(10'h1c1), .in3(10'h29f), .out(o12), .sel(idx));
  Multiplexer #(.select(2), .width(10)) multiplexer_16 (
    .in0(10'h60), .in1(10'h43), .in2(10'h1), .in3(10'h108), .out(o16), .sel(idx));
endmodule
